// Logisim project Oefening3.circ as structural Verilog: 1 circuit, main circuit main
module main (
  input  in_1,
  input  in_2,
  input  in_3,
  input  in_4,
  input  in_5,
  input  in_6,
  input  in_7,
  output out_8,
  output out_9,
  output out_10,
  output out_11
);

  wire and_1_out, and_2_out, and_3_out, and_4_out, and_5_out, and_6_out, and_7_out, not_2_out, not_4_out,
       not_5_out;

  and and_1 (and_1_out, in_1, in_2);
  and and_2 (and_2_out, in_3, in_4);
  and and_3 (and_3_out, in_5, in_5);
  and and_4 (and_4_out, in_6, in_6);
  and and_5 (and_5_out, in_7, in_7);
  not not_1 (out_8, and_1_out);
  not not_2 (not_2_out, and_2_out);
  not not_3 (out_10, and_3_out);
  not not_4 (not_4_out, and_4_out);
  not not_5 (not_5_out, and_5_out);
  and and_6 (and_6_out, not_2_out, not_2_out);
  not not_6 (out_9, and_6_out);
  and and_7 (and_7_out, not_4_out, not_5_out);
  not not_7 (out_11, and_7_out);

  // Notes on the sheet:
  //   OR using NAND's
  //   NAND using AND, NOT
  //   AND using NAND's
  //   NOT using NAND's
endmodule
