// Logisim project Oefening2.circ as structural Verilog: 2 circuits, main circuit CR
module CR (
  input  Start_Carry,
  input  [11:0] B,
  input  [11:0] A,
  output [11:0] out_4,
  output out_5
);

  wire n1b_adder_1_c_out, n1b_adder_2_c_out, n1b_adder_3_c_out, n1b_adder_4_c_out, n1b_adder_5_c_out,
       n1b_adder_6_c_out, n1b_adder_7_c_out, n1b_adder_8_c_out, n1b_adder_9_c_out, n1b_adder_10_c_out,
       n1b_adder_11_c_out;

  _1b_adder u_1b_adder_1 (.a(B[0]), .b(A[0]), .C_in(Start_Carry), .C_out(n1b_adder_1_c_out), .s(out_4[0]));
  _1b_adder u_1b_adder_2 (.a(B[1]), .b(A[1]), .C_in(n1b_adder_1_c_out), .C_out(n1b_adder_2_c_out), .s(out_4[1]));
  _1b_adder u_1b_adder_3 (.a(B[2]), .b(A[2]), .C_in(n1b_adder_2_c_out), .C_out(n1b_adder_3_c_out), .s(out_4[2]));
  _1b_adder u_1b_adder_4 (.a(B[3]), .b(A[3]), .C_in(n1b_adder_3_c_out), .C_out(n1b_adder_4_c_out), .s(out_4[3]));
  _1b_adder u_1b_adder_5 (.a(B[4]), .b(A[4]), .C_in(n1b_adder_4_c_out), .C_out(n1b_adder_5_c_out), .s(out_4[4]));
  _1b_adder u_1b_adder_6 (.a(B[5]), .b(A[5]), .C_in(n1b_adder_5_c_out), .C_out(n1b_adder_6_c_out), .s(out_4[5]));
  _1b_adder u_1b_adder_7 (.a(B[6]), .b(A[6]), .C_in(n1b_adder_6_c_out), .C_out(n1b_adder_7_c_out), .s(out_4[6]));
  _1b_adder u_1b_adder_8 (.a(B[7]), .b(A[7]), .C_in(n1b_adder_7_c_out), .C_out(n1b_adder_8_c_out), .s(out_4[7]));
  _1b_adder u_1b_adder_9 (.a(B[8]), .b(A[8]), .C_in(n1b_adder_8_c_out), .C_out(n1b_adder_9_c_out), .s(out_4[8]));
  _1b_adder u_1b_adder_10 (.a(B[9]), .b(A[9]), .C_in(n1b_adder_9_c_out), .C_out(n1b_adder_10_c_out), .s(out_4[9]));
  _1b_adder u_1b_adder_11 (.a(B[10]), .b(A[10]), .C_in(n1b_adder_10_c_out), .C_out(n1b_adder_11_c_out), .s(out_4[10]));
  _1b_adder u_1b_adder_12 (.a(B[11]), .b(A[11]), .C_in(n1b_adder_11_c_out), .C_out(out_5), .s(out_4[11]));

  // Notes on the sheet:
  //   <- Final Carry Out
endmodule

module _1b_adder (
  input  a,
  input  b,
  input  C_in,
  output s,
  output C_out
);

  wire and_1_out, and_2_out, xor_1_out;

  xor xor_1 (xor_1_out, a, b);
  and and_1 (and_1_out, xor_1_out, C_in);
  and and_2 (and_2_out, a, b);
  xor xor_2 (s, xor_1_out, C_in);
  or or_1 (C_out, and_1_out, and_2_out);
endmodule
