// Logisim project Oefening4.circ as structural Verilog: 1 circuit, main circuit main
module main (
  input  in_1,
  input  [11:0] in_2,
  input  [11:0] in_3,
  output [11:0] out_4,
  output out_5,
  output [11:0] out_6,
  output out_7
);

  CR cr_1 (.Start_Carry(in_1), .out_5(out_5), .B(in_2), .A(in_3), .out_4(out_4));
  // _12bCLA 12bcla_1: pin names not known; wires that end beside it: in_1, in_2, in_3, out_7, out_6
endmodule
